# Fritzing sketch arduino-brain-machine (saved by Fritzing 0.9.2b)
breadboards: 1

parts:
  Part1 = Arduino Uno (Rev3) - ICSP
  J1 = Screw terminal - 2 pins [package=THT]
  VCC1 = Battery block 9V
  R1 = Resistor [tolerance=±5% resistance=100 package="2512 [SMD]"]
  R2 = Resistor [tolerance=±5% resistance=100 package="2512 [SMD]"]
  Left_Eye = LEDs [package=led10mm]
  Right_Eye = LEDs [package=led10mm]
  R3 = Resistor [tolerance=±5% resistance=3.3k package="2512 [SMD]"]
  R4 = Resistor [tolerance=±5% resistance=3.3k package="2512 [SMD]"]
  Part2 = TRRS 3.5mm Jack Breakout
  C2 = Tantalum Capacitor [capacitance="1 μF" package="D 7343 [SMD, tantalum]"]
  C3 = Tantalum Capacitor [capacitance="1 μF" package="D 7343 [SMD, tantalum]"]
  R5 = Resistor [tolerance=±5% resistance=10k package="2512 [SMD]"]
  S1 = Momentary Switch [package=ksa_sealed_tac_switch]

nets:
  N1: Part1.5V, Left_Eye.C, Right_Eye.C, R5.Pin_1
  GND: Part1.GND, J1.pin2, VCC1.-, Part2.RING2, S1.1, S1.2
  N2: Part1.D9_PWM, R3.Pin_1
  N3: Part1.D10_PWM/SS, R4.Pin_1
  N4: Part1.D3_PWM, R5.Pin_0, S1.3, S1.4
  N5: Part1.D5_PWM, R1.Pin_1
  N6: Part1.D6_PWM, R2.Pin_1
  N7: Part1.VIN, J1.pin1, VCC1.+
  N8: R1.Pin_0, Left_Eye.A
  N9: R2.Pin_0, Right_Eye.A
  N10: R3.Pin_0, C2.+
  N11: R4.Pin_0, C3.+
  N12: Part2.RING1, C2.-
  N13: Part2.TIP, C3.-
